# Fritzing sketch Platine_ESP32TDMX_V1 (saved by Fritzing 1.0.7)
circuit board: 6.61821cm x 5.77781cm
breadboards: 1

parts:
  MAX485 = MAX485 Breakout LB Version [package=THT]
  ESP32 = ESP 32 DEVKIT DOIT
  POWER = screw terminal, 2 pins
  DMX = screw terminal, 4 pins
  BUCK_CONVERTER_5V = Mini-360 DC-DC Buck converter [package=THT]

nets:
  N1: MAX485.RE, MAX485.DE
  N2: MAX485.DI, ESP32.D2
  N3: MAX485.GND, ESP32.GND#16, DMX.pin1
  N4: MAX485.A, DMX.pin3
  N5: MAX485.B, DMX.pin2
  N6: MAX485.VCC, ESP32.Vin#15
  N7: ESP32.VP, ESP32.GND#13, ESP32.Vin#14, BUCK_CONVERTER_5V.OUT+, BUCK_CONVERTER_5V.OUT-
  N8: POWER.pin1, BUCK_CONVERTER_5V.IN-
  N9: POWER.pin2, BUCK_CONVERTER_5V.IN+

notes:
  ESP32TDMX V1 | made by Luca-Bke
  1    2    3
  +    -

custom parts:
  MAX485 Breakout LB Version: MAX485 RS485 breakout board
  Mini-360 DC-DC Buck converter: Mini-360 DC-DC Buck converter. Tiny buck step down voltage converter, input voltage 4.75 to 23V output 1 to 17V adjustable. Available from ebay and the like.
